// Logisim project 8bit_ALU.circ as structural Verilog
// Tunnel(A)
module FULL_ADDER (
  input  A,
  input  B,
  input  Cin,
  output Sum,
  output Carry
);

  wire and_1_out, and_2_out, and_3_out, or_1_out, xor_1_out;

  xor xor_1 (xor_1_out, A, B);
  and and_1 (and_1_out, A, B);
  and and_2 (and_2_out, A, Cin);
  and and_3 (and_3_out, B, Cin);
  or or_1 (or_1_out, and_1_out, and_2_out);
  xor xor_2 (Sum, xor_1_out, Cin);
  or or_2 (Carry, or_1_out, and_3_out);
endmodule

module RIPPLE_ADDER_8bit (
  input  [7:0] A,
  input  Cin,
  input  [7:0] B,
  output [7:0] Sum,
  output Cout
);

  wire FA0_carry, FA1_carry, FA2_carry, FA3_carry, FA4_carry, FA5_carry, FA6_carry;

  FULL_ADDER FA0 (.A(A[0]), .B(B[0]), .Cin(Cin), .Sum(Sum[0]), .Carry(FA0_carry));
  FULL_ADDER FA1 (.A(A[1]), .B(B[1]), .Cin(FA0_carry), .Sum(Sum[1]), .Carry(FA1_carry));
  FULL_ADDER FA2 (.A(A[2]), .B(B[2]), .Cin(FA1_carry), .Sum(Sum[2]), .Carry(FA2_carry));
  FULL_ADDER FA3 (.A(A[3]), .B(B[3]), .Cin(FA2_carry), .Sum(Sum[3]), .Carry(FA3_carry));
  FULL_ADDER FA4 (.A(A[4]), .B(B[4]), .Cin(FA3_carry), .Sum(Sum[4]), .Carry(FA4_carry));
  FULL_ADDER FA5 (.A(A[5]), .B(B[5]), .Cin(FA4_carry), .Sum(Sum[5]), .Carry(FA5_carry));
  FULL_ADDER FA6 (.A(A[6]), .B(B[6]), .Cin(FA5_carry), .Sum(Sum[6]), .Carry(FA6_carry));
  FULL_ADDER FA7 (.A(A[7]), .B(B[7]), .Cin(FA6_carry), .Sum(Sum[7]), .Carry(Cout));
endmodule

module ADDER_SUBTRACTOR (
  input  [7:0] A,
  input  [7:0] B,
  input  SUB,
  output [7:0] Sum,
  output Cout
);

  wire [7:0] xor_1_out;

  xor xor_1 (xor_1_out[0], B[0], SUB);
  xor xor_2 (xor_1_out[1], B[1], SUB);
  xor xor_3 (xor_1_out[2], B[2], SUB);
  xor xor_4 (xor_1_out[3], B[3], SUB);
  xor xor_5 (xor_1_out[4], B[4], SUB);
  xor xor_6 (xor_1_out[5], B[5], SUB);
  xor xor_7 (xor_1_out[6], B[6], SUB);
  xor xor_8 (xor_1_out[7], B[7], SUB);
  RIPPLE_ADDER_8bit ripple_adder_8bit_1 (.A(A), .Cin(SUB), .B(xor_1_out), .Sum(Sum), .Cout(Cout));
endmodule

module LOGIC_UNIT (
  input  [7:0] A,
  input  [7:0] B,
  output [7:0] AND_GATE,
  output [7:0] OR_GATE,
  output [7:0] XOR_GATE,
  output [7:0] NOT_GATE
);

  assign AND_GATE = A & B;  // AND_Gate and_1, 8 bits wide
  assign OR_GATE = A | B;  // OR_Gate or_1, 8 bits wide
  assign XOR_GATE = A ^ B;  // XOR_Gate xor_1, 8 bits wide
  assign NOT_GATE = ~A;  // NOT_Gate not_1, 8 bits wide
endmodule

module SHIFT_UNIT (
  input  [7:0] A,
  output [7:0] LSL_OUT,
  output [7:0] LSR_OUT,
  output [7:0] ASR_OUT
);

  Shifter shifter_1 (.in(A), .\dist (3'b001), .out(LSL_OUT));
  Shifter #(.shift("lr")) shifter_2 (.in(A), .\dist (3'b001), .out(LSR_OUT));
  Shifter #(.shift("ar")) shifter_3 (.in(A), .\dist (3'b001), .out(ASR_OUT));
endmodule

module MAIN_ALU (
  input  [7:0] A,
  input  [7:0] B,
  input  [3:0] Opcode,
  output [7:0] Result,
  output N,
  output Z,
  output CF
);

  wire adder_subtractor_1_cout, adder_subtractor_2_cout, DEC_cout, INC_cout, or_1_out;
  wire [7:0] adder_subtractor_1_sum, adder_subtractor_2_sum, DEC_sum, INC_sum, logic_unit_1_and_gate,
       logic_unit_1_not_gate, logic_unit_1_or_gate, logic_unit_1_xor_gate, shift_unit_1_asr_out,
       shift_unit_1_lsl_out, shift_unit_1_lsr_out;

  LOGIC_UNIT logic_unit_1 (
    .A(A), .B(B), .AND_GATE(logic_unit_1_and_gate), .OR_GATE(logic_unit_1_or_gate),
    .XOR_GATE(logic_unit_1_xor_gate), .NOT_GATE(logic_unit_1_not_gate));
  ADDER_SUBTRACTOR adder_subtractor_1 (
    .A(A), .B(B), .SUB(1'b0), .Sum(adder_subtractor_1_sum), .Cout(adder_subtractor_1_cout));
  ADDER_SUBTRACTOR adder_subtractor_2 (
    .A(A), .B(B), .SUB(1'b1), .Sum(adder_subtractor_2_sum), .Cout(adder_subtractor_2_cout));
  SHIFT_UNIT shift_unit_1 (
    .A(A), .LSL_OUT(shift_unit_1_lsl_out), .LSR_OUT(shift_unit_1_lsr_out), .ASR_OUT(shift_unit_1_asr_out));
  ADDER_SUBTRACTOR INC (.A(A), .B(8'h1), .SUB(1'b0), .Sum(INC_sum), .Cout(INC_cout));
  ADDER_SUBTRACTOR DEC (.A(A), .B(8'h1), .SUB(1'b1), .Sum(DEC_sum), .Cout(DEC_cout));
  Multiplexer #(.select(4), .width(8)) multiplexer_1 (
    .in0(INC_sum), .in1(DEC_sum), .in2(adder_subtractor_1_sum), .in3(adder_subtractor_2_sum),
    .in4(logic_unit_1_and_gate), .in5(logic_unit_1_or_gate), .in6(logic_unit_1_xor_gate),
    .in7(logic_unit_1_not_gate), .in8(shift_unit_1_lsl_out), .in9(shift_unit_1_lsr_out),
    .in10(shift_unit_1_asr_out), .in11(A), .out({N, Result[6:0]}), .sel(Opcode));  // open: in12, in13, in14, in15
  Multiplexer #(.select(4)) multiplexer_2 (
    .in0(adder_subtractor_1_cout), .in1(adder_subtractor_2_cout), .in2(1'b0), .in3(1'b0), .in4(1'b0),
    .in5(1'b0), .in6(1'b0), .in7(1'b0), .in8(1'b0), .in9(INC_cout), .in10(DEC_cout), .in11(1'b0),
    .in12(1'b0), .in13(1'b0), .in14(1'b0), .in15(1'b0), .out(CF), .sel(Opcode));
  or or_1 (or_1_out, N, Result[6], Result[5], Result[4], Result[3], Result[2], Result[1], Result[0]);
  not not_1 (Z, or_1_out);

  assign Result[7] = N;
endmodule
